# Fritzing sketch AutomaticWateringSystem (saved by Fritzing 1.0.6)
circuit board: 8.46667cm x 5.64444cm
breadboards: 1

parts:
  A1 = Esp32-c3 super mini
  Part1 = Dual MOSFETs PWM Module
  3_3V_to_ESP32 = RioRand LM2596
  12V_IN_PSU = Screw terminal - 2 pins [package=THT]
  12V_IN1_PSU = Screw terminal - 2 pins [package=THT]
  VALVE1 = Plastic Solenoid Valve
  Chirp!_Soil_Moisture_Sensor1 = Chirp! Soil Moisture Sensor v2.7.3
  R1 = Resistor [package="2512 [SMD]"]

nets (from the breadboard view):
  N1: A1.Pin_11, Part1.TRIG/PWM
  N2: A1.Pin_13, Chirp!_Soil_Moisture_Sensor1.pin_3
  N3: A1.Pin_14, 3_3V_to_ESP32.Pin_3, Chirp!_Soil_Moisture_Sensor1.Pin_1
  N4: A1.Pin_15, Part1.GND, 3_3V_to_ESP32.Pin_2, 3_3V_to_ESP32.Pin_4, 12V_IN_PSU.pin1, Chirp!_Soil_Moisture_Sensor1.pin_5
  N5: Part1.+VLOAD, 12V_IN1_PSU.pin1
  N6: Part1.-VLOAD, 12V_IN1_PSU.pin2
  N7: Part1.-VIN, VALVE1.no_name_yet#1, R1.Pin_0
  N8: Part1.+VIN, VALVE1.no_name_yet#2, R1.Pin_1
  N9: 3_3V_to_ESP32.Pin_1, 12V_IN_PSU.pin2

custom parts:
  Esp32-c3 super mini: ESP32-C3 Development Board ESP32 SuperMini Development Board ESP32 Development Board WiFi Bluetooth.
  Dual MOSFETs PWM Module: Dual Mosfet PWM Module
  Resistor: Resistor Basic schematic elements and footprints for 0603, 1206, and PTH resistors.

// code stored in the sketch: automatic_watering_system.bas
digitalWrite(GPIO2, HIGH);
